# Fritzing sketch ApproxyClock (saved by Fritzing 0.8.7b)
circuit board: 16cm x 10cm
breadboards: 2

parts:
  VCC1 = 4 x AAA Battery Mount
  A1 = atmega328 [package=dip]
  C2 = Capacitor [package=cap-pth-small2]
  C1 = Capacitor [package=cap-pth-small2]
  Y1 = CRYSTAL [package=crystal-smd-10.5x4.8-2pin]
  LED1 = RGB LED (com. cathode, rbg) [package="5 mm [THT]"]
  LED2 = RGB LED (com. cathode, rbg) [package="5 mm [THT]"]
  R1 = Resistor [tolerance=±5% resistance=1k package=THT]
  R2 = Resistor [tolerance=±5% resistance=1k package=THT]
  R3 = Resistor [tolerance=±5% resistance=1k package=THT]
  R4 = Resistor [tolerance=±5% resistance=1k package=THT]
  R5 = Resistor [tolerance=±5% resistance=1k package=THT]
  R6 = Resistor [tolerance=±5% resistance=1k package=THT]
  RT2S1 = Resistor [tolerance=±5% resistance=1k package=THT]
  RT1S1 = Resistor [tolerance=±5% resistance=1k package=THT]
  RT1H1 = Resistor [tolerance=±5% resistance=1M package=THT]
  TR1 = Resistor [tolerance=±5% resistance=0 package=THT]
  TL1 = Resistor [tolerance=±5% resistance=0 package=THT]
  RT2H1 = Resistor [tolerance=±5% resistance=1M package=THT]

nets:
  N1: VCC1.-, A1.GND, C2.2, C1.2, LED1.common_cathode, LED2.common_cathode
  N2: VCC1.+, A1.VCC, A1.AVCC, A1.AREF
  N3: A1.D2, RT1S1.Pin_1, RT1H1.Pin_0
  N4: A1.D3_(PWM), R2.Pin_0
  N5: A1.D4, RT1H1.Pin_1, RT2H1.Pin_0
  N6: A1.XLAT1, C1.1, Y1.1
  N7: A1.XLAT2, C2.1, Y1.2
  N8: A1.D5_(PWM), R1.Pin_0
  N9: A1.D6_(PWM), R3.Pin_0
  N10: A1.D7, RT2S1.Pin_1, RT2H1.Pin_1
  N11: A1.D9_(PWM), R6.Pin_0
  N12: A1.D10_(PWM), R4.Pin_0
  N13: A1.D11_(PWM), R5.Pin_0
  N14: LED1.red_anode, R1.Pin_1
  N15: LED1.blue_anode, R2.Pin_1
  N16: LED1.green_anode, R3.Pin_1
  N17: LED2.red_anode, R4.Pin_1
  N18: LED2.blue_anode, R6.Pin_1
  N19: LED2.green_anode, R5.Pin_1
  N20: RT2S1.Pin_0, TR1.Pin_0
  N21: RT1S1.Pin_0, TL1.Pin_1

notes:
  Capacitors: 22 pF
  Crystal: 16 MHz
  Followed the same wiring as the RGB LED supplied by Fritzing, which is not the RGB LED I use
